// Logisim project 2 bit multiplier.circ as structural Verilog: 1 circuit, main circuit main
module main (
  input  B1,
  input  B0,
  input  A1,
  input  A0,
  output R0,
  output R1,
  output R2,
  output R3
);

  wire and_1_out, and_2_out, and_3_out, main_1_c;

  and and_1 (and_1_out, A1, B0);
  and and_2 (and_2_out, A0, B1);
  and and_3 (and_3_out, A1, B1);
  and and_4 (R0, A0, B0);
  half_adderr_main main_1 (.x(and_1_out), .y(and_2_out), .s(R1), .c(main_1_c));
  half_adderr_main main_2 (.x(main_1_c), .y(and_3_out), .s(R2), .c(R3));

  // Notes on the sheet:
  //   2-bit multiplier
endmodule
