// Logisim project 2by4 decoder.circ as structural Verilog: 1 circuit, main circuit main
module main (
  input  A,
  input  B,
  output D0,
  output D1,
  output D2,
  output D3
);

  wire not_1_out, not_2_out;

  not not_1 (not_1_out, A);
  not not_2 (not_2_out, B);
  and A_prime_B_prime (D0, not_1_out, not_2_out);
  and A_prime_B (D1, not_1_out, B);
  and AB_prime (D2, A, not_2_out);
  and AB (D3, A, B);

  // Notes on the sheet:
  //   2*4 decoder
endmodule
