// Logisim project 3-bit multiplier.circ as structural Verilog: 1 circuit, main circuit main
module main (
  input  B2,
  input  A2,
  input  B1,
  input  A1,
  input  B0,
  input  A0,
  output R0,
  output R1,
  output R2,
  output R3,
  output R4,
  output R5
);

  wire and_2_out, and_3_out, and_4_out, and_5_out, and_6_out, and_7_out, and_8_out, and_9_out, and_10_out,
       and_11_out, and_13_out, xor_2_out;

  and and_1 (R0, A0, B0);
  and and_2 (and_2_out, A1, B0);
  and and_3 (and_3_out, B1, A0);
  and and_4 (and_4_out, A2, B0);
  and and_5 (and_5_out, A1, B1);
  and and_6 (and_6_out, A0, B2);
  and and_7 (and_7_out, A2, B1);
  and and_8 (and_8_out, A1, B2);
  and and_9 (and_9_out, A2, B1);
  xor xor_1 (R1, and_2_out, and_3_out);
  and and_10 (and_10_out, and_2_out, and_3_out);
  xor xor_2 (xor_2_out, and_7_out, and_8_out);
  and and_11 (and_11_out, and_13_out, and_7_out, and_8_out);
  xor xor_3 (R4, and_11_out, and_9_out);
  and and_12 (R5, and_11_out, and_9_out);
  ExactlyOne xor_4 (.out(R2), .in0(and_10_out), .in1(and_4_out), .in2(and_5_out), .in3(and_6_out));
  and and_13 (and_13_out, and_10_out, and_4_out, and_5_out, and_6_out);
  xor xor_5 (R3, and_13_out, xor_2_out);
endmodule
