// Logisim project 3567mux4by1ABsel.circ as structural Verilog: 1 circuit, main circuit main
module main (
  input  B,
  input  C,
  input  A,
  output Y
);

  _4by1Mux_main main_1 (.i0(1'b0), .i1(C), .i2(C), .i3(1'b1), .A(A), .B(B), .Y(Y));
endmodule
