// Logisim project 3bitmajorityckybydecoder.circ as structural Verilog: 1 circuit, main circuit main
module main (
  input  Y,
  input  X,
  input  Z,
  output C,
  output S
);

  wire main_1_d0, main_1_d1, main_1_d2, main_1_d3, main_1_d4, main_1_d5, main_1_d6, main_1_d7;

  _3by8_decoder_main main_1 (
    .A(X), .B(Y), .C(Z), .D0(main_1_d0), .D1(main_1_d1), .D2(main_1_d2), .D3(main_1_d3), .D4(main_1_d4),
    .D5(main_1_d5), .D6(main_1_d6), .D7(main_1_d7));
  or or_1 (C, main_1_d0, main_1_d1, main_1_d2, main_1_d4);
  or or_2 (S, main_1_d3, main_1_d5, main_1_d6, main_1_d7);

  // Notes on the sheet:
  //   3bit majority decoder
endmodule
