// Logisim project 3by8 decoder.circ as structural Verilog: 1 circuit, main circuit main
module main (
  input  A,
  input  B,
  input  C,
  output D0,
  output D1,
  output D2,
  output D3,
  output D4,
  output D5,
  output D6,
  output D7
);

  wire not_1_out, not_2_out, not_3_out;

  not not_1 (not_1_out, A);
  not not_2 (not_2_out, B);
  not not_3 (not_3_out, C);
  and A_prime_B_prime_C_prime (D0, not_1_out, not_2_out, not_3_out);
  and A_prime_B_prime_C (D1, not_1_out, not_2_out, C);
  and A_prime_BC_prime (D2, not_1_out, B, not_3_out);
  and A_prime_BC (D3, not_1_out, not_2_out, not_3_out);
  and AB_prime_C_prime (D4, A, not_2_out, not_3_out);
  and AB_prime_C (D5, A, not_2_out, C);
  and ABC_prime (D6, A, B, not_3_out);
  and ABC (D7, A, B, C);

  // Notes on the sheet:
  //   3*8 Decoder
endmodule
