// Logisim project 4BBFA.circ as structural Verilog: 1 circuit, main circuit main
module main (
  input  X3,
  input  X2,
  input  X1,
  input  X0,
  input  Y3,
  input  y2,
  input  Y1,
  input  Y0,
  output Cy,
  output S3,
  output S2,
  output S1,
  output S0
);

  wire main_2_c, main_3_c, main_4_c;

  FULL_ADDER_main main_1 (.X(main_2_c), .Y(X3), .Z(Y3), .S(S3), .C(Cy));
  FULL_ADDER_main main_2 (.X(main_3_c), .Y(X2), .Z(y2), .S(S2), .C(main_2_c));
  FULL_ADDER_main main_3 (.X(main_4_c), .Y(X1), .Z(Y1), .S(S1), .C(main_3_c));
  half_adderr_main main_4 (.x(X0), .y(Y0), .s(S0), .c(main_4_c));

  // Notes on the sheet:
  //   binary parallel adder
endmodule
