// Logisim project 4by1Mux.circ as structural Verilog: 1 circuit, main circuit main
module main (
  input  A,
  input  B,
  input  i0,
  input  i1,
  input  i2,
  input  i3,
  output Y
);

  wire and_1_out, and_2_out, and_3_out, and_4_out, not_1_out, not_2_out;

  not not_1 (not_1_out, A);
  not not_2 (not_2_out, B);
  and and_1 (and_1_out, not_1_out, not_2_out, i0);
  and and_2 (and_2_out, not_1_out, B, i1);
  and and_3 (and_3_out, A, not_2_out, i2);
  and and_4 (and_4_out, A, B, i3);
  or or_1 (Y, and_1_out, and_2_out, and_3_out, and_4_out);

  // Notes on the sheet:
  //   4*1 mux
endmodule
