// Logisim project 8by1mux.circ as structural Verilog: 1 circuit, main circuit main
module main (
  input  A,
  input  B,
  input  C,
  input  i0,
  input  i1_prime,
  input  i2,
  input  i3,
  input  i4,
  input  i5,
  input  i6,
  input  i7,
  output Y
);

  wire and_1_out, and_2_out, and_3_out, and_4_out, and_5_out, and_6_out, and_7_out, and_8_out, not_1_out,
       not_2_out, not_3_out;

  not not_1 (not_1_out, A);
  not not_2 (not_2_out, B);
  not not_3 (not_3_out, C);
  and and_1 (and_1_out, i0, not_1_out, not_2_out, not_3_out);
  and and_2 (and_2_out, i1_prime, not_1_out, not_2_out, C);
  and and_3 (and_3_out, i2, not_1_out, B, not_3_out);
  and and_4 (and_4_out, i3, not_1_out, B, C);
  and and_5 (and_5_out, i4, A, not_2_out, not_3_out);
  and and_6 (and_6_out, i5, A, not_2_out, C);
  and and_7 (and_7_out, i6, A, B, not_3_out);
  and and_8 (and_8_out, i7, A, B, C);
  or or_1 (Y, and_1_out, and_2_out, and_3_out, and_4_out, and_5_out, and_6_out, and_7_out, and_8_out);

  // Notes on the sheet:
  //   8*1MUx
endmodule
