// Logisim project ABCDusing8by1mux.circ as structural Verilog: 1 circuit, main circuit main
module main (
  input  D,
  input  C,
  input  A,
  input  B,
  output Y
);

  wire not_1_out;

  not not_1 (not_1_out, D);
  _8by1mux_main main_1 (
    .i0(1'b1), .i1_prime(not_1_out), .i2(1'b0), .i3(D), .i4(1'b1), .i5(1'b0), .i6(1'b1), .i7(D), .A(A),
    .B(B), .C(C), .Y(Y));
endmodule
