// Logisim project FA using HA.circ as structural Verilog: 1 circuit, main circuit main
module main (
  input  X,
  input  Y,
  input  Z,
  output S,
  output C
);

  wire main_1_c, main_1_s, main_2_c;

  half_adderr_main main_1 (.x(X), .y(Y), .s(main_1_s), .c(main_1_c));
  half_adderr_main main_2 (.x(main_1_s), .y(Z), .s(S), .c(main_2_c));
  or or_1 (C, main_2_c, main_1_c);

  // Notes on the sheet:
  //   full adder using HA
endmodule
