// Logisim project FS using HS.circ as structural Verilog: 1 circuit, main circuit main
module main (
  input  X,
  input  Y,
  input  Z,
  output D,
  output B
);

  wire main_1_b, main_1_d, main_2_b;

  hs_main main_1 (.X(X), .Y(Y), .D(main_1_d), .B(main_1_b));
  hs_main main_2 (.X(main_1_d), .Y(Z), .D(D), .B(main_2_b));
  or or_1 (B, main_2_b, main_1_b);

  // Notes on the sheet:
  //   Full Subtractor using HS
endmodule
