// Logisim project FULL ADDER.circ as structural Verilog: 1 circuit, main circuit main
module main (
  input  X,
  input  Y,
  input  Z,
  output S,
  output C
);

  wire and_1_out, and_2_out, xor_2_out;

  ExactlyOne xor_1 (.out(S), .in0(X), .in1(Y), .in2(Z));
  and and_1 (and_1_out, X, Y);
  xor xor_2 (xor_2_out, X, Y);
  and and_2 (and_2_out, xor_2_out, Z);
  or or_1 (C, and_1_out, and_2_out);

  // Notes on the sheet:
  //   FULL ADDER
endmodule
