// Logisim project bcd adder.circ as structural Verilog: 1 circuit, main circuit main
module main (
  input  X2,
  input  Y3,
  input  Y0,
  input  X1,
  input  Y2,
  input  X0,
  input  Y1,
  input  X3,
  output S2,
  output S3,
  output S0,
  output S1,
  output carrry
);

  wire and_1_out, and_2_out, main_1_cy, main_1_s0, main_1_s1, main_1_s2, main_1_s3, or_1_out;

  or or_1 (or_1_out, and_1_out, main_1_cy, and_2_out);
  and and_1 (and_1_out, main_1_s3, main_1_s2);
  and and_2 (and_2_out, main_1_s3, main_1_s1);
  _4BBFA_main main_1 (
    .Y3(Y3), .X3(X3), .y2(Y2), .X2(X2), .Y1(Y1), .X1(X1), .Y0(Y0), .X0(X0), .Cy(main_1_cy), .S3(main_1_s3),
    .S2(main_1_s2), .S1(main_1_s1), .S0(main_1_s0));
  _4BBFA_main main_2 (
    .Y3(1'b0), .X3(main_1_s3), .y2(or_1_out), .X2(main_1_s2), .Y1(or_1_out), .X1(main_1_s1), .Y0(1'b0),
    .X0(main_1_s0), .Cy(carrry), .S3(S3), .S2(S2), .S1(S1), .S0(S0));

  // Notes on the sheet:
  //   BCD ADDER
endmodule
