// Logisim project decowithena.circ as structural Verilog: 1 circuit, main circuit main
module main (
  input  A,
  input  B,
  input  E,
  output D0,
  output D1,
  output D2,
  output D3
);

  wire not_1_out, not_2_out;

  not not_1 (not_1_out, A);
  not not_2 (not_2_out, B);
  and A_prime_B_prime_E (D0, E, not_2_out, not_1_out);
  and A_prime_BE (D1, E, B, not_1_out);
  and AB_prime_E (D2, A, not_2_out, E);
  and ABE (D3, A, B, E);

  // Notes on the sheet:
  //   decoder with enable
endmodule
