// Logisim project fs.circ as structural Verilog: 1 circuit, main circuit main
module main (
  input  X,
  input  Y,
  input  Z,
  output D,
  output B
);

  wire and_1_out, and_2_out, not_1_out, xnor_1_out;

  not not_1 (not_1_out, X);
  ExactlyOne xor_1 (.out(D), .in0(X), .in1(Y), .in2(Z));
  and and_1 (and_1_out, not_1_out, Y);
  xnor xnor_1 (xnor_1_out, X, Y);
  and and_2 (and_2_out, xnor_1_out, Z);
  or or_1 (B, and_1_out, and_2_out);

  // Notes on the sheet:
  //   Full Subtractor
endmodule
