// Logisim project half adderr.circ as structural Verilog: 1 circuit, main circuit main
module main (
  input  x,
  input  y,
  output s,
  output c
);

  xor xor_1 (s, x, y);
  and and_1 (c, x, y);

  // Notes on the sheet:
  //   half adder
endmodule
