// Logisim project hs.circ as structural Verilog: 1 circuit, main circuit main
module main (
  input  X,
  input  Y,
  output D,
  output B
);

  wire not_1_out;

  not not_1 (not_1_out, X);
  xor xor_1 (D, X, Y);
  and and_1 (B, not_1_out, Y);

  // Notes on the sheet:
  //   Half Subtractor
endmodule
