// Logisim project majoority8bymux.circ as structural Verilog: 1 circuit, main circuit main
module main (
  input  B,
  input  C,
  input  A,
  output Y
);

  _8by1mux_main main_1 (
    .i0(1'b0), .i1_prime(1'b0), .i2(1'b0), .i3(1'b1), .i4(1'b0), .i5(1'b1), .i6(1'b1), .i7(1'b1), .A(A),
    .B(B), .C(C), .Y(Y));
endmodule
