// Logisim project srfffusinnor.circ as structural Verilog: 1 circuit, main circuit main
module main (
  input  S,
  input  R,
  output Q_prime,
  output Q
);

  nor nor_1 (Q_prime, S, Q);
  nor nor_2 (Q, Q_prime, R);
endmodule
