// Logisim project traficlight.circ as structural Verilog: 1 circuit, main circuit main
module main (
  input  E
);

  wire and_1_out, and_2_out, clock_1_out, d_ff_1_q, d_ff_1_qn, d_ff_2_q, d_ff_2_qn;

  Clock clock_1 (.out(clock_1_out));
  D_Flip_Flop d_ff_1 (.clk(clock_1_out), .D(d_ff_1_qn), .Q(d_ff_1_q), .Qn(d_ff_1_qn), .en(E));  // open: preset, reset
  D_Flip_Flop d_ff_2 (.clk(d_ff_1_qn), .D(d_ff_2_qn), .Q(d_ff_2_q), .Qn(d_ff_2_qn), .en(E));  // open: preset, reset
  and and_1 (and_1_out, d_ff_1_qn, d_ff_2_qn);
  and and_2 (and_2_out, d_ff_1_qn, d_ff_2_q);
  LED led_1 (.in(and_1_out));
  LED led_2 (.in(d_ff_1_q));
  LED led_3 (.in(and_2_out));

  // Notes on the sheet:
  //   Traffic Light
endmodule
